# Fritzing sketch TinkurCompass Wiring Diagram (saved by Fritzing 0.8.7b)

parts:
  BREAKOUT1 = HMC5883L Compass Breakout
  Part1 = Arduino Uno (Rev3) - ICSP
  LED1 = 8x8 LED Matrix (green)

nets:
  N1: BREAKOUT1.SCL, Part1.A5/SCL, LED1.C
  N2: BREAKOUT1.SDA, BREAKOUT1.3vo, Part1.A4/SDA, LED1.D
  GND: BREAKOUT1.GND, Part1.GND, LED1.-
  VIN: BREAKOUT1.VIN, Part1.5V, LED1.+

custom parts:
  8x8 LED Matrix (green): 8x8 LED Matrix with I2C control (green)
